# Fritzing sketch Weather Station (saved by Fritzing 0.9.3b)
breadboards: 2

parts:
  Part1 = KY-008 Laser Transmitter Module [package="Breakout board"]
  BT1 = Bluetooth HC-06u [package=THT]
  Part2 = Arduino Nano (Rev3.0)
  Part3 = Solar Cell  # not connected
  BATT1 = LiPoly Battery (1300mAh)  # not connected
  Part4 = Adafruit USB LiIon/LiPoly Charger [part_number="Adafruit #259"]  # not connected

nets:
  N1: Part1.S, Part2.D3
  GND: Part1.-, BT1.GND, Part2.GND
  VCC: BT1.VCC, Part2.5V
  N2: BT1.TXD, Part2.D4
  N3: BT1.RXD, Part2.D5

notes:
  Lithium Battery
  Lipo Rider V1.3

custom parts:
  KY-008 Laser Transmitter Module: Laser Transmitter module KY-008 for Arduino, emits a dot shaped red laser beam.
  Bluetooth HC-06u: Bluetooth HC-06 - face up, pins down 16.5mm x 37.5mm PCB
  LiPoly Battery (1300mAh): Lithium Ion Polymer Battery (1300mAh)
  Adafruit USB LiIon/LiPoly Charger: This is a Lithium Ion and Lithium Polymer battery charger based on the MCP73833. It uses a USB mini-B for connection to any computer or 'USB wall adapter'. Charging is performed in three stages: first a preconditioning charge, then a constant-current fast charge and finally a constant-voltage trickle charge to keep the battery topped-up. The fast-charge current is 500mA by default, but is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
